# Fritzing sketch digisense-bme280 (saved by Fritzing 0.9.3b)
breadboards: 1

parts:
  U1 = NodeMCU V1.0
  R1 = Photocell (LDR) [package=THT]
  R2 = Resistor [tolerance=±5% resistance=10k package="1206 [SMD]"]
  Part1 = GY-BMEP280 Barometric Pressure Sensor - Breakout

nets:
  N1: U1.D1, Part1.SCL
  N2: U1.D2, Part1.SDA
  3V3: U1.3V3, R1.pin_1, Part1.VCC
  GND: U1.GND, R2.Pin_1, Part1.GND
  N3: U1.A0, R1.pin_0, R2.Pin_0

custom parts:
  NodeMCU V1.0: ESP8266 based NodeMCU
  GY-BMEP280 Barometric Pressure Sensor - Breakout: The BME280 is a chip which was originally designed for the next generation of smartphones. It is made up of a very accurate pressure sensor and an associated temperature sensor which helps calibrate the pressure readings. And just for fun they threw in a pretty solid humidity sensor in there as well! So with an I2C connection you have access to enough weather data to make some pretty good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
